# Fritzing sketch Reloj_Digital (saved by Fritzing 0.9.3b)
breadboards: 1

parts:
  Componente1 = Arduino Uno (Rev3)
  U3 = LCD-16X2 [package=lcd-16x2]
  R1 = TRIMPOT [package=trim_pot_pth]
  Componente2 = Bluetooth HC-05 Macho
  S1 = Pushbutton [package="[SMD]"]
  S2 = Pushbutton [package="[SMD]"]
  S3 = Pushbutton [package="[SMD]"]
  R2 = Resistor [tolerance=±5% resistance=220 package="0805 [SMD]"]
  R3 = Resistor [tolerance=±5% resistance=220 package="0805 [SMD]"]
  R4 = Resistor [tolerance=±5% resistance=220 package="0805 [SMD]"]

nets:
  N1: Componente1.D9_PWM, S2.Pin_3, S2.Pin_4
  N2: Componente1.D12/MISO, S3.Pin_3, S3.Pin_4
  GND: Componente1.GND, U3.VSS, U3.R_W, U3.K, R1.CCW, Componente2.GND, R3.Pin_1, R4.Pin_1
  N3: Componente1.D0/RX, Componente2.TXD
  N4: Componente1.D1/TX, Componente2.RXD
  N5: Componente1.D2, U3.RS
  N6: Componente1.D3_PWM, U3.E
  N7: Componente1.D4, U3.DB4
  N8: Componente1.D5_PWM, U3.DB5
  N9: Componente1.D6_PWM, U3.DB6
  N10: Componente1.D7, U3.DB7
  5V: Componente1.5V, U3.VDD, U3.A, R1.CW, Componente2.VCC
  N11: U3.VO, R1.WIPER
  N12: S1.Pin_1, S1.Pin_2, R2.Pin_0
  N13: S1.Pin_3, S1.Pin_4
  N14: S2.Pin_1, S2.Pin_2, R3.Pin_0
  N15: S3.Pin_1, S3.Pin_2, R4.Pin_0
